# Fritzing sketch pcb buttons-midibreakout (saved by Fritzing 0.9.2b)
circuit board: 3.50308cm x 2.79277cm
breadboards: 1

parts:
  vcc_gnd_tx = Generic female header - 3 pins [form="♀ (female)" package=THT]
  in_2_&_4 = Generic female header - 2 pins [form="♀ (female)" package=MNK]
  GND_VCC = female pin header, 2 pins [form="♀ (female)"]
  D1 = Diode [package=diode-1n4148]
  6n137 = IC, DIP package, 8 pins [chip_label=IC]
  R3 = Resistor [tolerance=±5% resistance=220 package=THT]
  R2 = Resistor [tolerance=±5% resistance=220 package=THT]
  R1 = Resistor [tolerance=±5% resistance=220 package=THT]
  R4 = Resistor [tolerance=±5% resistance=10k package=THT]
  rx_tx = female pin header, 2 pins [form="♀ (female)"]

nets:
  N1: vcc_gnd_tx.pin1, R1.Pin_0
  GND: vcc_gnd_tx.pin2, GND_VCC.pin1, 6n137.pin5
  N2: vcc_gnd_tx.pin3, R2.Pin_0
  N3: in_2_&_4.Pin_1, R3.Pin_0
  N4: in_2_&_4.pin2, D1.A, 6n137.pin3
  N5: GND_VCC.pin2, 6n137.pin8, R1.Pin_1, R4.Pin_0
  N6: D1.C, 6n137.pin2, R3.Pin_1
  N7: 6n137.pin6, R4.Pin_1, rx_tx.pin2
  N8: R2.Pin_1, rx_tx.pin1

custom parts:
  Generic female header - 3 pins: MIDI OUT PORT
  Generic female header - 2 pins: MIDI IN HEADER
